// Logisim project 1_zadanie_cederle_marek_logisim.circ as structural Verilog: 1 circuit, main circuit main
module main (
  input  A,
  input  B,
  input  C,
  input  D,
  output Y_zad,
  output Z_zad,
  output Y_DNF,
  output Z_DNF,
  output Y_KNF,
  output Z_KNF
);

  wire A_B_out, B_C_out, B_D_out, B_nC_nD_out, C_D_nA_out, C_D_nB_out, C_D_out, C_nD_2_out, C_nD_out,
       D_nB_nC_out, D_nC_out, nA_nB_out, nA_nC_nD_out, nB_C_out, nB_nC_nD_out, not_1_out, not_2_out,
       not_3_out, not_4_out, not_5_out, not_6_out, not_7_out, not_8_out, not_9_out;

  not not_1 (not_1_out, D);
  not not_2 (not_2_out, D);
  not not_3 (not_3_out, C);
  not not_4 (not_4_out, A);
  not not_5 (not_5_out, B);
  not not_6 (not_6_out, A);
  not not_7 (not_7_out, B);
  not not_8 (not_8_out, C);
  not not_9 (not_9_out, D);
  xor C_nD (C_nD_out, C, not_1_out);
  and B_D (B_D_out, B, D);
  and C_nD_2 (C_nD_2_out, C, not_2_out);
  and D_nC (D_nC_out, D, not_3_out);
  and nA_nB (nA_nB_out, not_4_out, not_5_out);
  and B_C (B_C_out, B, C);
  and D_nB_nC (D_nB_nC_out, D, not_5_out, not_3_out);
  or A_B (A_B_out, A, B);
  or C_D_nA (C_D_nA_out, C, D, not_6_out);
  or C_D_nB (C_D_nB_out, C, D, not_7_out);
  or nA_nC_nD (nA_nC_nD_out, not_6_out, not_8_out, not_9_out);
  or nB_nC_nD (nB_nC_nD_out, not_7_out, not_8_out, not_9_out);
  or nB_C (nB_C_out, not_7_out, C);
  or B_nC_nD (B_nC_nD_out, B, not_8_out, not_9_out);
  or C_D (C_D_out, C, D);
  nand n__A_B___C_nD (Y_zad, A_B_out, C_nD_out);
  xnor n__C_nD___B_D (Z_zad, C_nD_out, B_D_out);
  or C_nD___D_nC___nA_nB (Y_DNF, C_nD_2_out, D_nC_out, nA_nB_out);
  or B_C___C_nD___D_nB_nC (Z_DNF, B_C_out, C_nD_2_out, D_nB_nC_out);
  and C_D_nA___C_D_nB___nA_nC_nD___nB_nC_nD (Y_KNF, C_D_nA_out, C_D_nB_out, nA_nC_nD_out, nB_nC_nD_out);
  and nB_C___B_nC_nD___C_D (Z_KNF, nB_C_out, B_nC_nD_out, C_D_out);
endmodule
