// Logisim project 2_zad-cederle-marek-logisim.circ as structural Verilog: 1 circuit, main circuit main
module main (
  input  a,
  input  b,
  input  c,
  input  d,
  output A_D,
  output B_D,
  output C_D,
  output D_D,
  output A_K,
  output B_K,
  output C_K,
  output D_K
);

  wire n_a_c_d_out, n_a_nd_out, n_b_c_out, n_b_d_out, n_b_nd_out, n_na_b_d_out, n_na_c_out, na_2_out, na_out,
       nb_out, nc_out, nd_2_out, nd_out;

  nand na (na_out, a, a);
  nor na_2 (na_2_out, a, a);
  nand nb (nb_out, b, b);
  nor nc (nc_out, c, c);
  nand nd (nd_out, d, d);
  nor nd_2 (nd_2_out, d, d);
  nand n_a_c_d (n_a_c_d_out, a, c, d);
  nand n_a_nd (n_a_nd_out, a, nd_out);
  nand n_na_c (n_na_c_out, na_out, c);
  nand n_b_c (n_b_c_out, b, c);
  nor n_b_d (n_b_d_out, b, d);
  nor n_b_nd (n_b_nd_out, b, nd_2_out);
  nor n_na_b_d (n_na_b_d_out, na_2_out, b, d);
  nand n_nb_n_a_c_d (A_D, nb_out, n_a_c_d_out);
  nand n_nb_n_a_nd (B_D, nb_out, n_a_nd_out);
  nand n_n_na_c__n_a_c_d__n_b_c (C_D, n_na_c_out, n_a_c_d_out, n_b_c_out);
  nor n_na_n_b_d (A_K, na_2_out, n_b_d_out);
  nor n_na_n_b_nd (B_K, na_2_out, n_b_nd_out);
  nor n_nc_n_na_b_d (C_K, nc_out, n_na_b_d_out);

  assign D_D = d;
  assign D_K = d;
endmodule
